// Logisim project ex3_3.circ as structural Verilog: 1 circuit, main circuit main
module main (
);

  wire and_1_out, not_1_out, not_2_out, or_1_out, x_out, y_out;

  Button x (.out(x_out));
  Button y (.out(y_out));
  not not_1 (not_1_out, x_out);
  and and_1 (and_1_out, not_1_out, y_out);
  not not_2 (not_2_out, y_out);
  or or_1 (or_1_out, and_1_out, not_2_out);
  LED led_1 (.in(or_1_out));
endmodule
